// Logisim project avx.circ as structural Verilog
// S_o
module main (
  input  [31:0] A_i,
  input  [31:0] B_i,
  input  mode_i,
  input  [1:0] vecSize_i,
  output [31:0] S_o
);

  Adder_Subtractor adder_subtractor_1 (.A_i(A_i), .B_i(B_i), .mode_i(mode_i), .vecSize_i(vecSize_i), .S_o(S_o));
endmodule

// VHDL entity Adder_Subtractor, as the project stores it:
library IEEE;
use IEEE.STD_LOGIC_1164.ALL;
use IEEE.STD_LOGIC_ARITH.ALL;
use IEEE.STD_LOGIC_UNSIGNED.ALL;

entity Adder_Subtractor is
    Port (
        A_i       : in  STD_LOGIC_VECTOR (31 downto 0);
        B_i       : in  STD_LOGIC_VECTOR (31 downto 0);
        mode_i    : in  STD_LOGIC; -- 0 para adicão, 1 para subtração
        vecSize_i : in  STD_LOGIC_VECTOR (1 downto 0); -- 00=4 bits, 01=8 bits, 10=16 bits, 11=32 bits
        S_o       : out STD_LOGIC_VECTOR (31 downto 0)
    );
end Adder_Subtractor;

architecture Behavioral of Adder_Subtractor is
    signal A, B, B_comp, B_mux, Sum : STD_LOGIC_VECTOR (31 downto 0);
begin

    -- Processo para ajustar os tamanhos dos vetores
    process(A_i, B_i, vecSize_i)
    begin
        case vecSize_i is
            when "00" =>
                A <= (31 downto 4 => '0') & A_i(3 downto 0);
                B <= (31 downto 4 => '0') & B_i(3 downto 0);
            when "01" =>
                A <= (31 downto 8 => '0') & A_i(7 downto 0);
                B <= (31 downto 8 => '0') & B_i(7 downto 0);
            when "10" =>
                A <= (31 downto 16 => '0') & A_i(15 downto 0);
                B <= (31 downto 16 => '0') & B_i(15 downto 0);
            when others =>
                A <= A_i;
                B <= B_i;
        end case;
    end process;

    -- Processo para definir o operando B baseado no modo (adição/subtração)
    process(B, mode_i)
    begin
        if mode_i = '1' then
            B_comp <= NOT B; -- Complemento de B
        else
            B_comp <= B;
        end if;
    end process;

    -- Mux para selecionar entre B e B_comp
    B_mux <= B_comp when mode_i = '1' else B;

    -- Adição/subtração
    process(A, B_mux, mode_i)
    begin
        if mode_i = '1' then
            -- Subtração
            Sum <= A + B_mux + "00000000000000000000000000000001"; -- Adiciona 1 para o complemento de 2
        else
            -- Adição
            Sum <= A + B_mux;
        end if;
    end process;

    -- Saída ajustada de acordo com o tamanho do vetor
    process(Sum, vecSize_i)
    begin
        case vecSize_i is
            when "00" =>
                S_o <= (31 downto 4 => '0') & Sum(3 downto 0);
            when "01" =>
                S_o <= (31 downto 8 => '0') & Sum(7 downto 0);
            when "10" =>
                S_o <= (31 downto 16 => '0') & Sum(15 downto 0);
            when others =>
                S_o <= Sum;
        end case;
    end process;

end Behavioral;
